// Logisim project ALU Test.circ as structural Verilog: 4 circuits, main circuit main
module main (
  input  [7:0] in_1,
  input  [7:0] in_2,
  output [7:0] out_3
);

  wire [3:0] n8b_4b_splitter_1_h, n8b_4b_splitter_1_l, n8b_4b_splitter_2_h, n8b_4b_splitter_2_l,
       n8b_4b_splitter_3_h, n8b_4b_splitter_3_l;

  Hex_Digit_Display hex_digit_display_1 (.value(n8b_4b_splitter_1_h));  // open: dp
  _8b_4b_Splitter u_8b_4b_splitter_1 (.in_1(in_1), .H(n8b_4b_splitter_1_h), .L(n8b_4b_splitter_1_l));
  Hex_Digit_Display hex_digit_display_2 (.value(n8b_4b_splitter_2_h));  // open: dp
  _8b_4b_Splitter u_8b_4b_splitter_2 (.in_1(in_2), .H(n8b_4b_splitter_2_h), .L(n8b_4b_splitter_2_l));
  Hex_Digit_Display hex_digit_display_3 (.value(n8b_4b_splitter_1_l));  // open: dp
  Hex_Digit_Display hex_digit_display_4 (.value(n8b_4b_splitter_2_l));  // open: dp
  _8b_ALU u_8b_alu_1 (.A(in_1), .B(in_2), .R(out_3));
  Hex_Digit_Display hex_digit_display_5 (.value(n8b_4b_splitter_3_l));  // open: dp
  Hex_Digit_Display hex_digit_display_6 (.value(n8b_4b_splitter_3_h));  // open: dp
  _8b_4b_Splitter u_8b_4b_splitter_3 (.in_1(out_3), .H(n8b_4b_splitter_3_h), .L(n8b_4b_splitter_3_l));
endmodule

module _1b_ALU (
  input  A,
  input  B,
  output Carry,
  output Result,
  output Equals
);

  and and_1 (Carry, A, B);
  xor xor_1 (Result, A, B);
  not not_1 (Equals, Result);
endmodule

module _8b_ALU (
  input  [7:0] A,
  input  [7:0] B,
  output [7:0] R
);

  wire n1b_alu_1_carry, n1b_alu_2_carry, n1b_alu_2_result, n1b_alu_3_carry, n1b_alu_3_result,
       n1b_alu_4_carry, n1b_alu_4_result, n1b_alu_5_carry, n1b_alu_5_result, n1b_alu_6_carry,
       n1b_alu_6_result, n1b_alu_7_carry, n1b_alu_7_result, n1b_alu_8_result, n1b_alu_9_carry,
       n1b_alu_10_carry, n1b_alu_10_result, n1b_alu_11_carry, n1b_alu_11_result, n1b_alu_12_carry,
       n1b_alu_12_result, n1b_alu_13_carry, n1b_alu_13_result, n1b_alu_14_carry, n1b_alu_14_result,
       n1b_alu_15_result, n1b_alu_16_carry, n1b_alu_17_carry, n1b_alu_17_result, n1b_alu_18_carry,
       n1b_alu_18_result, n1b_alu_19_carry, n1b_alu_19_result, n1b_alu_20_carry, n1b_alu_20_result,
       n1b_alu_21_result, n1b_alu_22_carry, n1b_alu_23_carry, n1b_alu_23_result, n1b_alu_24_carry,
       n1b_alu_24_result, n1b_alu_25_carry, n1b_alu_25_result, n1b_alu_26_result, n1b_alu_27_carry,
       n1b_alu_28_carry, n1b_alu_28_result, n1b_alu_29_carry, n1b_alu_29_result, n1b_alu_30_result,
       n1b_alu_31_carry, n1b_alu_32_carry, n1b_alu_32_result, n1b_alu_33_result, n1b_alu_34_carry,
       n1b_alu_35_result;

  _1b_ALU u_1b_alu_1 (.A(A[0]), .B(B[0]), .Carry(n1b_alu_1_carry), .Result(R[0]));  // open: Equals
  _1b_ALU u_1b_alu_2 (.A(A[1]), .B(B[1]), .Carry(n1b_alu_2_carry), .Result(n1b_alu_2_result));  // open: Equals
  _1b_ALU u_1b_alu_3 (.A(A[2]), .B(B[2]), .Carry(n1b_alu_3_carry), .Result(n1b_alu_3_result));  // open: Equals
  _1b_ALU u_1b_alu_4 (.A(A[3]), .B(B[3]), .Carry(n1b_alu_4_carry), .Result(n1b_alu_4_result));  // open: Equals
  _1b_ALU u_1b_alu_5 (.A(A[4]), .B(B[4]), .Carry(n1b_alu_5_carry), .Result(n1b_alu_5_result));  // open: Equals
  _1b_ALU u_1b_alu_6 (.A(A[5]), .B(B[5]), .Carry(n1b_alu_6_carry), .Result(n1b_alu_6_result));  // open: Equals
  _1b_ALU u_1b_alu_7 (.A(A[6]), .B(B[6]), .Carry(n1b_alu_7_carry), .Result(n1b_alu_7_result));  // open: Equals
  _1b_ALU u_1b_alu_8 (.A(A[7]), .B(B[7]), .Result(n1b_alu_8_result));  // open: Carry, Equals
  _1b_ALU u_1b_alu_9 (
    .A(n1b_alu_1_carry), .B(n1b_alu_2_result), .Carry(n1b_alu_9_carry), .Result(R[1]));  // open: Equals
  _1b_ALU u_1b_alu_10 (
    .A(n1b_alu_2_carry), .B(n1b_alu_3_result), .Carry(n1b_alu_10_carry), .Result(n1b_alu_10_result));  // open: Equals
  _1b_ALU u_1b_alu_11 (
    .A(n1b_alu_3_carry), .B(n1b_alu_4_result), .Carry(n1b_alu_11_carry), .Result(n1b_alu_11_result));  // open: Equals
  _1b_ALU u_1b_alu_12 (
    .A(n1b_alu_4_carry), .B(n1b_alu_5_result), .Carry(n1b_alu_12_carry), .Result(n1b_alu_12_result));  // open: Equals
  _1b_ALU u_1b_alu_13 (
    .A(n1b_alu_5_carry), .B(n1b_alu_6_result), .Carry(n1b_alu_13_carry), .Result(n1b_alu_13_result));  // open: Equals
  _1b_ALU u_1b_alu_14 (
    .A(n1b_alu_6_carry), .B(n1b_alu_7_result), .Carry(n1b_alu_14_carry), .Result(n1b_alu_14_result));  // open: Equals
  _1b_ALU u_1b_alu_15 (.A(n1b_alu_7_carry), .B(n1b_alu_8_result), .Result(n1b_alu_15_result));  // open: Carry, Equals
  _1b_ALU u_1b_alu_16 (
    .A(n1b_alu_9_carry), .B(n1b_alu_10_result), .Carry(n1b_alu_16_carry), .Result(R[2]));  // open: Equals
  _1b_ALU u_1b_alu_17 (
    .A(n1b_alu_10_carry), .B(n1b_alu_11_result), .Carry(n1b_alu_17_carry), .Result(n1b_alu_17_result));  // open: Equals
  _1b_ALU u_1b_alu_18 (
    .A(n1b_alu_11_carry), .B(n1b_alu_12_result), .Carry(n1b_alu_18_carry), .Result(n1b_alu_18_result));  // open: Equals
  _1b_ALU u_1b_alu_19 (
    .A(n1b_alu_12_carry), .B(n1b_alu_13_result), .Carry(n1b_alu_19_carry), .Result(n1b_alu_19_result));  // open: Equals
  _1b_ALU u_1b_alu_20 (
    .A(n1b_alu_13_carry), .B(n1b_alu_14_result), .Carry(n1b_alu_20_carry), .Result(n1b_alu_20_result));  // open: Equals
  _1b_ALU u_1b_alu_21 (.A(n1b_alu_14_carry), .B(n1b_alu_15_result), .Result(n1b_alu_21_result));  // open: Carry, Equals
  _1b_ALU u_1b_alu_22 (
    .A(n1b_alu_16_carry), .B(n1b_alu_17_result), .Carry(n1b_alu_22_carry), .Result(R[3]));  // open: Equals
  _1b_ALU u_1b_alu_23 (
    .A(n1b_alu_17_carry), .B(n1b_alu_18_result), .Carry(n1b_alu_23_carry), .Result(n1b_alu_23_result));  // open: Equals
  _1b_ALU u_1b_alu_24 (
    .A(n1b_alu_18_carry), .B(n1b_alu_19_result), .Carry(n1b_alu_24_carry), .Result(n1b_alu_24_result));  // open: Equals
  _1b_ALU u_1b_alu_25 (
    .A(n1b_alu_19_carry), .B(n1b_alu_20_result), .Carry(n1b_alu_25_carry), .Result(n1b_alu_25_result));  // open: Equals
  _1b_ALU u_1b_alu_26 (.A(n1b_alu_20_carry), .B(n1b_alu_21_result), .Result(n1b_alu_26_result));  // open: Carry, Equals
  _1b_ALU u_1b_alu_27 (
    .A(n1b_alu_22_carry), .B(n1b_alu_23_result), .Carry(n1b_alu_27_carry), .Result(R[4]));  // open: Equals
  _1b_ALU u_1b_alu_28 (
    .A(n1b_alu_23_carry), .B(n1b_alu_24_result), .Carry(n1b_alu_28_carry), .Result(n1b_alu_28_result));  // open: Equals
  _1b_ALU u_1b_alu_29 (
    .A(n1b_alu_24_carry), .B(n1b_alu_25_result), .Carry(n1b_alu_29_carry), .Result(n1b_alu_29_result));  // open: Equals
  _1b_ALU u_1b_alu_30 (.A(n1b_alu_25_carry), .B(n1b_alu_26_result), .Result(n1b_alu_30_result));  // open: Carry, Equals
  _1b_ALU u_1b_alu_31 (
    .A(n1b_alu_27_carry), .B(n1b_alu_28_result), .Carry(n1b_alu_31_carry), .Result(R[5]));  // open: Equals
  _1b_ALU u_1b_alu_32 (
    .A(n1b_alu_28_carry), .B(n1b_alu_29_result), .Carry(n1b_alu_32_carry), .Result(n1b_alu_32_result));  // open: Equals
  _1b_ALU u_1b_alu_33 (.A(n1b_alu_29_carry), .B(n1b_alu_30_result), .Result(n1b_alu_33_result));  // open: Carry, Equals
  _1b_ALU u_1b_alu_34 (
    .A(n1b_alu_31_carry), .B(n1b_alu_32_result), .Carry(n1b_alu_34_carry), .Result(R[6]));  // open: Equals
  _1b_ALU u_1b_alu_35 (.A(n1b_alu_32_carry), .B(n1b_alu_33_result), .Result(n1b_alu_35_result));  // open: Carry, Equals
  _1b_ALU u_1b_alu_36 (.A(n1b_alu_34_carry), .B(n1b_alu_35_result), .Result(R[7]));  // open: Carry, Equals
endmodule

module _8b_4b_Splitter (
  input  [7:0] in_1,
  output [3:0] H,
  output [3:0] L
);


  assign H = in_1[7:4];
  assign L = in_1[3:0];
endmodule
