// Logisim project Example_A1.circ as structural Verilog: 1 circuit, main circuit main
module main (
  input  in_1,
  input  in_2
);

  wire and_1_out, nand_1_out, or_1_out;

  or or_1 (or_1_out, in_1, in_2);
  nand nand_1 (nand_1_out, in_1, in_2);
  and and_1 (and_1_out, or_1_out, nand_1_out);
  LED led_1 (.in(and_1_out));

  // Other names for the same wires on the sheet: A = in_1; B = in_2
endmodule
