// Logisim project clock.circ as structural Verilog: 7 circuits, main circuit main
module main (
  output [3:0] out_1,
  output [3:0] out_2,
  output [3:0] out_3,
  output [3:0] out_4,
  output [3:0] out_5,
  output [3:0] out_6
);

  wire button_1_out, button_2_out, button_3_out, n4bit7segmentdecoder_1_a, n4bit7segmentdecoder_1_b,
       n4bit7segmentdecoder_1_c, n4bit7segmentdecoder_1_d, n4bit7segmentdecoder_1_e,
       n4bit7segmentdecoder_1_f, n4bit7segmentdecoder_1_g, n4bit7segmentdecoder_1_p,
       n4bit7segmentdecoder_2_a, n4bit7segmentdecoder_2_b, n4bit7segmentdecoder_2_c,
       n4bit7segmentdecoder_2_d, n4bit7segmentdecoder_2_e, n4bit7segmentdecoder_2_f,
       n4bit7segmentdecoder_2_g, n4bit7segmentdecoder_2_p, n4bit7segmentdecoder_3_a,
       n4bit7segmentdecoder_3_b, n4bit7segmentdecoder_3_c, n4bit7segmentdecoder_3_d,
       n4bit7segmentdecoder_3_e, n4bit7segmentdecoder_3_f, n4bit7segmentdecoder_3_g,
       n4bit7segmentdecoder_3_p, n4bit7segmentdecoder_4_a, n4bit7segmentdecoder_4_b,
       n4bit7segmentdecoder_4_c, n4bit7segmentdecoder_4_d, n4bit7segmentdecoder_4_e,
       n4bit7segmentdecoder_4_f, n4bit7segmentdecoder_4_g, n4bit7segmentdecoder_4_p,
       n4bit7segmentdecoder_5_a, n4bit7segmentdecoder_5_b, n4bit7segmentdecoder_5_c,
       n4bit7segmentdecoder_5_d, n4bit7segmentdecoder_5_e, n4bit7segmentdecoder_5_f,
       n4bit7segmentdecoder_5_g, n4bit7segmentdecoder_5_p, n4bit7segmentdecoder_6_a,
       n4bit7segmentdecoder_6_b, n4bit7segmentdecoder_6_c, n4bit7segmentdecoder_6_d,
       n4bit7segmentdecoder_6_e, n4bit7segmentdecoder_6_f, n4bit7segmentdecoder_6_g,
       n4bit7segmentdecoder_6_p, not_1_out, T0_out;
  wire [3:0] clocksettings_1_mode_2;
  wire [15:0] clocksettings_1_t_plus, time_1_t;

  Button T0 (.out(T0_out));
  ClockSettings clocksettings_1 (
    .T(time_1_t), .Set(button_2_out), .DEL(button_3_out), .Mode(button_1_out),
    .T_plus(clocksettings_1_t_plus), .Mode_2(clocksettings_1_mode_2));
  Time time_1 (.T(time_1_t), .DEL(T0_out));
  Button button_1 (.out(button_1_out));
  Button button_2 (.out(button_2_out));
  Button button_3 (.out(button_3_out));
  Hours hours_1 (.T(clocksettings_1_t_plus), .HE(out_2), .HT(out_1));
  Minutes minutes_1 (.T(clocksettings_1_t_plus), .MT(out_3), .ME(out_4));
  Seconds seconds_1 (.T(clocksettings_1_t_plus), .ST(out_5), .SE(out_6));
  _4bit7SegmentDecoder u_4bit7segmentdecoder_1 (
    .Point(clocksettings_1_mode_2[0]), .N(out_1), .a(n4bit7segmentdecoder_1_a), .b(n4bit7segmentdecoder_1_b),
    .c(n4bit7segmentdecoder_1_c), .d(n4bit7segmentdecoder_1_d), .e(n4bit7segmentdecoder_1_e),
    .f(n4bit7segmentdecoder_1_f), .g(n4bit7segmentdecoder_1_g), .p(n4bit7segmentdecoder_1_p));
  _7_Segment_Display u_7_segment_display_1 (
    .g(n4bit7segmentdecoder_1_f), .f(n4bit7segmentdecoder_1_g), .a(n4bit7segmentdecoder_1_a),
    .b(n4bit7segmentdecoder_1_b), .e(n4bit7segmentdecoder_1_e), .d(n4bit7segmentdecoder_1_d),
    .c(n4bit7segmentdecoder_1_c), .dp(n4bit7segmentdecoder_1_p));
  _4bit7SegmentDecoder u_4bit7segmentdecoder_2 (
    .Point(clocksettings_1_mode_2[0]), .N(out_2), .a(n4bit7segmentdecoder_2_a), .b(n4bit7segmentdecoder_2_b),
    .c(n4bit7segmentdecoder_2_c), .d(n4bit7segmentdecoder_2_d), .e(n4bit7segmentdecoder_2_e),
    .f(n4bit7segmentdecoder_2_f), .g(n4bit7segmentdecoder_2_g), .p(n4bit7segmentdecoder_2_p));
  _7_Segment_Display u_7_segment_display_2 (
    .g(n4bit7segmentdecoder_2_f), .f(n4bit7segmentdecoder_2_g), .a(n4bit7segmentdecoder_2_a),
    .b(n4bit7segmentdecoder_2_b), .e(n4bit7segmentdecoder_2_e), .d(n4bit7segmentdecoder_2_d),
    .c(n4bit7segmentdecoder_2_c), .dp(n4bit7segmentdecoder_2_p));
  _4bit7SegmentDecoder u_4bit7segmentdecoder_3 (
    .Point(clocksettings_1_mode_2[1]), .N(out_3), .a(n4bit7segmentdecoder_3_a), .b(n4bit7segmentdecoder_3_b),
    .c(n4bit7segmentdecoder_3_c), .d(n4bit7segmentdecoder_3_d), .e(n4bit7segmentdecoder_3_e),
    .f(n4bit7segmentdecoder_3_f), .g(n4bit7segmentdecoder_3_g), .p(n4bit7segmentdecoder_3_p));
  _4bit7SegmentDecoder u_4bit7segmentdecoder_4 (
    .Point(clocksettings_1_mode_2[1]), .N(out_4), .a(n4bit7segmentdecoder_4_a), .b(n4bit7segmentdecoder_4_b),
    .c(n4bit7segmentdecoder_4_c), .d(n4bit7segmentdecoder_4_d), .e(n4bit7segmentdecoder_4_e),
    .f(n4bit7segmentdecoder_4_f), .g(n4bit7segmentdecoder_4_g), .p(n4bit7segmentdecoder_4_p));
  _7_Segment_Display u_7_segment_display_3 (
    .g(n4bit7segmentdecoder_4_f), .f(n4bit7segmentdecoder_4_g), .a(n4bit7segmentdecoder_4_a),
    .b(n4bit7segmentdecoder_4_b), .e(n4bit7segmentdecoder_4_e), .d(n4bit7segmentdecoder_4_d),
    .c(n4bit7segmentdecoder_4_c), .dp(n4bit7segmentdecoder_4_p));
  _7_Segment_Display u_7_segment_display_4 (
    .g(n4bit7segmentdecoder_3_f), .f(n4bit7segmentdecoder_3_g), .a(n4bit7segmentdecoder_3_a),
    .b(n4bit7segmentdecoder_3_b), .e(n4bit7segmentdecoder_3_e), .d(n4bit7segmentdecoder_3_d),
    .c(n4bit7segmentdecoder_3_c), .dp(n4bit7segmentdecoder_3_p));
  LED led_1 (.in(not_1_out));
  LED led_2 (.in(not_1_out));
  not not_1 (not_1_out, clocksettings_1_mode_2[3]);
  _4bit7SegmentDecoder u_4bit7segmentdecoder_5 (
    .Point(clocksettings_1_mode_2[2]), .N(out_5), .a(n4bit7segmentdecoder_5_a), .b(n4bit7segmentdecoder_5_b),
    .c(n4bit7segmentdecoder_5_c), .d(n4bit7segmentdecoder_5_d), .e(n4bit7segmentdecoder_5_e),
    .f(n4bit7segmentdecoder_5_f), .g(n4bit7segmentdecoder_5_g), .p(n4bit7segmentdecoder_5_p));
  _7_Segment_Display u_7_segment_display_5 (
    .g(n4bit7segmentdecoder_5_f), .f(n4bit7segmentdecoder_5_g), .a(n4bit7segmentdecoder_5_a),
    .b(n4bit7segmentdecoder_5_b), .e(n4bit7segmentdecoder_5_e), .d(n4bit7segmentdecoder_5_d),
    .c(n4bit7segmentdecoder_5_c), .dp(n4bit7segmentdecoder_5_p));
  LED led_3 (.in(not_1_out));
  LED led_4 (.in(not_1_out));
  _4bit7SegmentDecoder u_4bit7segmentdecoder_6 (
    .Point(clocksettings_1_mode_2[2]), .N(out_6), .a(n4bit7segmentdecoder_6_a), .b(n4bit7segmentdecoder_6_b),
    .c(n4bit7segmentdecoder_6_c), .d(n4bit7segmentdecoder_6_d), .e(n4bit7segmentdecoder_6_e),
    .f(n4bit7segmentdecoder_6_f), .g(n4bit7segmentdecoder_6_g), .p(n4bit7segmentdecoder_6_p));
  _7_Segment_Display u_7_segment_display_6 (
    .g(n4bit7segmentdecoder_6_f), .f(n4bit7segmentdecoder_6_g), .a(n4bit7segmentdecoder_6_a),
    .b(n4bit7segmentdecoder_6_b), .e(n4bit7segmentdecoder_6_e), .d(n4bit7segmentdecoder_6_d),
    .c(n4bit7segmentdecoder_6_c), .dp(n4bit7segmentdecoder_6_p));

  // Notes on the sheet:
  //   Mode
  //   Set
  //   Del
endmodule

module Hours (
  input  [15:0] T,
  output [3:0] HT,
  output [3:0] HE
);

  wire [15:0] divider_1_out, divider_2_out, divider_3_rem, divider_4_out, divider_4_rem;

  Divider #(.width(16)) divider_1 (.a(T), .b(16'h3c), .out(divider_1_out));  // open: upper, rem
  Divider #(.width(16)) divider_2 (.a(divider_1_out), .b(16'h3c), .out(divider_2_out));  // open: upper, rem
  Divider #(.width(16)) divider_3 (.a(divider_2_out), .b(16'h18), .rem(divider_3_rem));  // open: out, upper
  Divider #(.width(16)) divider_4 (
    .a(divider_3_rem), .b(16'ha), .out(divider_4_out), .rem(divider_4_rem));  // open: upper
  Bit_Extender #(.in_width(16), .out_width(4)) bit_extender_1 (.in(divider_4_out), .out(HT));
  Bit_Extender #(.in_width(16), .out_width(4)) bit_extender_2 (.in(divider_4_rem), .out(HE));
endmodule

module Time (
  input  DEL,
  output [15:0] T
);

  wire clock_1_out;
  wire [15:0] adder_1_out, bit_extender_1_out;

  Clock clock_1 (.out(clock_1_out));
  assign bit_extender_1_out = {{15{1'b0}}, clock_1_out};  // Bit_Extender bit_extender_1
  Adder #(.width(16)) adder_1 (.a(T), .b(bit_extender_1_out), .out(adder_1_out));  // open: cin, cout
  Register #(.width(16), .trigger("falling")) register_1 (
    .D(adder_1_out), .Q(T), .clk(clock_1_out), .clr(DEL));  // open: en
endmodule

module Minutes (
  input  [15:0] T,
  output [3:0] MT,
  output [3:0] ME
);

  wire [15:0] divider_1_out, divider_2_rem, divider_3_out, divider_3_rem;

  Divider #(.width(16)) divider_1 (.a(T), .b(16'h3c), .out(divider_1_out));  // open: upper, rem
  Divider #(.width(16)) divider_2 (.a(divider_1_out), .b(16'h3c), .rem(divider_2_rem));  // open: out, upper
  Divider #(.width(16)) divider_3 (
    .a(divider_2_rem), .b(16'ha), .out(divider_3_out), .rem(divider_3_rem));  // open: upper
  Bit_Extender #(.in_width(16), .out_width(4)) bit_extender_1 (.in(divider_3_out), .out(MT));
  Bit_Extender #(.in_width(16), .out_width(4)) bit_extender_2 (.in(divider_3_rem), .out(ME));
endmodule

module Seconds (
  input  [15:0] T,
  output [3:0] ST,
  output [3:0] SE
);

  wire [15:0] divider_1_rem, divider_2_out, divider_2_rem;

  Divider #(.width(16)) divider_1 (.a(T), .b(16'h3c), .rem(divider_1_rem));  // open: out, upper
  Divider #(.width(16)) divider_2 (
    .a(divider_1_rem), .b(16'ha), .out(divider_2_out), .rem(divider_2_rem));  // open: upper
  Bit_Extender #(.in_width(16), .out_width(4)) bit_extender_1 (.in(divider_2_out), .out(ST));
  Bit_Extender #(.in_width(16), .out_width(4)) bit_extender_2 (.in(divider_2_rem), .out(SE));
endmodule

module _4bit7SegmentDecoder (
  input  Point,
  input  [3:0] N,
  output a,
  output b,
  output c,
  output d,
  output e,
  output f,
  output g,
  output p
);

  wire _0_out, _1_out, _2_out, _3_out, _4_out, _5_out, _6_out, _7_out, _8_out, _9_out, not_1_out, not_2_out,
       not_3_out, not_4_out, not_5_out, not_6_out, not_7_out, not_8_out, not_9_out, not_10_out, not_11_out,
       not_12_out, not_13_out;

  Hex_Digit_Display hex_digit_display_1 (.value(N), .dp(Point));
  not not_1 (not_1_out, N[0]);
  not not_2 (not_2_out, N[1]);
  not not_3 (not_3_out, N[2]);
  not not_4 (not_4_out, N[3]);
  not not_5 (not_5_out, N[2]);
  not not_6 (not_6_out, N[1]);
  not not_7 (not_7_out, N[3]);
  not not_8 (not_8_out, N[0]);
  not not_9 (not_9_out, N[3]);
  not not_10 (not_10_out, N[3]);
  not not_11 (not_11_out, N[3]);
  not not_12 (not_12_out, N[1]);
  not not_13 (not_13_out, N[2]);
  nor _0 (_0_out, N[0], N[1], N[2], N[3]);
  nor _1 (_1_out, not_1_out, N[1], N[2], N[3]);
  nor _2 (_2_out, N[0], not_2_out, N[2], N[3]);
  and _3 (_3_out, N[0], N[1], not_3_out, not_4_out);
  nor _4 (_4_out, N[0], N[1], not_5_out, N[3]);
  and _5 (_5_out, N[0], not_6_out, N[2], not_7_out);
  and _6 (_6_out, not_8_out, N[1], N[2], not_9_out);
  and _7 (_7_out, N[0], N[1], N[2], not_10_out);
  nor _8 (_8_out, N[0], N[1], N[2], not_11_out);
  and _9 (_9_out, N[0], not_12_out, not_13_out, N[3]);
  or or_1 (a, _0_out, _2_out, _3_out, _5_out, _6_out, _7_out, _8_out, _9_out);
  or or_2 (b, _0_out, _1_out, _2_out, _3_out, _4_out, _7_out, _8_out, _9_out);
  or or_3 (c, _0_out, _1_out, _3_out, _4_out, _5_out, _6_out, _7_out, _8_out, _9_out);
  or or_4 (d, _0_out, _2_out, _3_out, _5_out, _6_out, _8_out, _9_out);
  or or_5 (e, _0_out, _2_out, _6_out, _8_out);
  or or_6 (f, _2_out, _3_out, _4_out, _5_out, _6_out, _8_out, _9_out);
  or or_7 (g, _0_out, _4_out, _5_out, _6_out, _8_out, _9_out);
  _7_Segment_Display u_7_segment_display_1 (.g(f), .f(g), .a(a), .b(b), .e(e), .d(d), .c(c), .dp(Point));

  assign p = Point;
endmodule

module ClockSettings (
  input  [15:0] T,
  input  Set,
  input  DEL,
  input  Mode,
  output [15:0] T_plus,
  output [3:0] Mode_2
);

  wire and_1_out, and_2_out, and_3_out, clock_1_out, d_ff_3_qn, or_2_out;
  wire [15:0] adder_1_out, bit_extender_1_out, bit_extender_2_out, bit_extender_3_out, multiplier_1_out,
       multiplier_2_out, or_1_out, register_1_q;

  and and_1 (and_1_out, Mode_2[0], Set);
  and and_2 (and_2_out, Mode_2[1], Set);
  and and_3 (and_3_out, Mode_2[2], Set);
  D_Flip_Flop d_ff_1 (.clk(Mode), .D(d_ff_3_qn), .Q(Mode_2[0]), .reset(Mode_2[1]));  // open: Qn, preset, en
  assign bit_extender_1_out = {{15{1'b0}}, and_1_out};  // Bit_Extender bit_extender_1
  assign bit_extender_2_out = {{15{1'b0}}, and_2_out};  // Bit_Extender bit_extender_2
  assign bit_extender_3_out = {{15{1'b0}}, and_3_out};  // Bit_Extender bit_extender_3
  Multiplier #(.width(16)) multiplier_1 (
    .a(bit_extender_1_out), .b(16'he10), .out(multiplier_1_out));  // open: cin, cout
  Multiplier #(.width(16)) multiplier_2 (
    .a(bit_extender_2_out), .b(16'h3c), .out(multiplier_2_out));  // open: cin, cout
  D_Flip_Flop d_ff_2 (.clk(Mode), .D(Mode_2[0]), .Q(Mode_2[1]));  // open: Qn, preset, en, reset
  D_Flip_Flop d_ff_3 (.clk(Mode), .D(Mode_2[1]), .Q(Mode_2[2]), .Qn(d_ff_3_qn));  // open: preset, en, reset
  assign or_1_out = multiplier_1_out | multiplier_2_out | bit_extender_3_out;  // OR_Gate or_1, 16 bits wide
  Adder #(.width(16)) adder_1 (.a(register_1_q), .b(or_1_out), .out(adder_1_out));  // open: cin, cout
  Adder #(.width(16)) adder_2 (.a(T), .b(register_1_q), .out(T_plus));  // open: cin, cout
  Register #(.width(16), .trigger("falling")) register_1 (
    .D(adder_1_out), .Q(register_1_q), .clk(Set), .clr(DEL));  // open: en
  or or_2 (or_2_out, Mode_2[0], Mode_2[1], Mode_2[2]);
  Clock clock_1 (.out(clock_1_out));
  and and_4 (Mode_2[3], or_2_out, clock_1_out);

  // Other names for the same wires on the sheet: ph = Mode_2[0]; pm = Mode_2[1]; ps = Mode_2[2]
endmodule
