// Logisim project io_test.circ as structural Verilog: 1 circuit, main circuit main
module main (
  input  A,
  input  B,
  output F,
  output C,
  output T
);

  wire B_out;

  Button u_B (.out(B_out));
  Clock clock_1 (.out(T));
  T_Flip_Flop t_ff_1 (.clk(B_out), .T(B_out), .Q(F));  // open: Qn, preset, reset, en
  xor xor_1 (C, A, B);
endmodule
