// Logisim project terminal.circ as structural Verilog: 1 circuit, main circuit main
module main (
);

  wire button_1_out, clock_1_out;
  wire [6:0] adder_1_out, bit_extender_1_out, register_1_q;

  Clock clock_1 (.out(clock_1_out));
  assign bit_extender_1_out = {{6{1'b0}}, clock_1_out};  // Bit_Extender bit_extender_1
  Adder #(.width(7)) adder_1 (.a(register_1_q), .b(bit_extender_1_out), .out(adder_1_out));  // open: cin, cout
  Register #(.width(7), .trigger("falling")) register_1 (
    .D(adder_1_out), .Q(register_1_q), .clk(clock_1_out));  // open: en, clr
  Button button_1 (.out(button_1_out));
  TTY tty_1 (.data(register_1_q), .clk(clock_1_out), .clr(button_1_out));  // open: we
endmodule
