// Logisim project xor.circ as structural Verilog: 1 circuit, main circuit main
module main (
  input  in_1,
  output out_2,
  output out_3
);

  wire B, nand_1_out, or_1_out;

  Clock clock_1 (.out(B));
  or or_1 (or_1_out, in_1, B);
  nand nand_1 (nand_1_out, in_1, B);
  xor xor_1 (out_3, out_2, B);
  and and_1 (out_2, or_1_out, nand_1_out);

  // Other names for the same wires on the sheet: A = in_1; C = out_2; D = out_3
endmodule
